// Logisim project a2023_s1_e1_p3.circ as structural Verilog: 3 circuits, main circuit main
module main (
  input  in_1,
  input  in_2,
  input  in_3,
  input  in_4,
  input  in_5,
  input  in_6,
  input  in_7,
  input  in_8,
  input  OR,
  input  in_10,
  output out_11,
  output out_12,
  output out_13,
  output out_14,
  output out_15,
  output out_16,
  output out_17,
  output out_18
);

  wire clock_1_out, nor_3_out, nor_4_out, nor_5_out;

  nor nor_1 (out_11, in_1, in_2);
  nor nor_2 (out_14, in_5, in_5);
  nor nor_3 (nor_3_out, in_7, in_7);
  nor nor_4 (nor_4_out, in_8, in_8);
  nor nor_5 (nor_5_out, OR, in_10);
  nor nor_6 (out_17, nor_3_out, nor_4_out);
  nor nor_7 (out_18, nor_5_out, nor_5_out);
  Clock clock_1 (.out(clock_1_out));
  rs_agreg rs_agreg_1 (.R(in_3), .S(in_4), .Q(out_12), .Qbar(out_13));
  d_agreg d_agreg_1 (.D(in_6), .H(clock_1_out), .Q(out_15), .Qbar(out_16));

  // Notes on the sheet:
  //   NOT
  //   AND
endmodule

module rs_agreg (
  input  R,
  input  S,
  output Q,
  output Qbar
);

  nor nor_1 (Q, R, Qbar);
  nor nor_2 (Qbar, Q, S);

  // Notes on the sheet:
  //   BASCULE RS
endmodule

module d_agreg (
  input  H,
  input  D,
  output Q,
  output Qbar
);

  wire or_1_out, rs_agreg_1_qbar, rs_agreg_2_q, rs_agreg_2_qbar;

  or or_1 (or_1_out, rs_agreg_1_qbar, H);
  rs_agreg rs_agreg_1 (.R(rs_agreg_2_qbar), .S(H), .Qbar(rs_agreg_1_qbar));  // open: Q
  rs_agreg rs_agreg_2 (.R(or_1_out), .S(D), .Q(rs_agreg_2_q), .Qbar(rs_agreg_2_qbar));
  rs_agreg rs_agreg_3 (.R(rs_agreg_1_qbar), .S(rs_agreg_2_q), .Q(Q), .Qbar(Qbar));

  // Notes on the sheet:
  //   BASCULE D
endmodule
