// Logisim project a2023_s1_e1_p3.circ as structural Verilog: 5 circuits, main circuit main
module main (
  input  in_1,
  input  in_2,
  input  in_3,
  input  in_4,
  input  in_5,
  input  in_6,
  input  in_7,
  input  in_8,
  input  OR,
  input  in_10,
  output out_11,
  output out_12,
  output out_13,
  output out_14,
  output out_15,
  output out_16,
  output out_17,
  output out_18
);

  wire clock_1_out, nor_3_out, nor_4_out, nor_5_out;

  nor nor_1 (out_11, in_1, in_2);
  nor nor_2 (out_14, in_5, in_5);
  nor nor_3 (nor_3_out, in_7, in_7);
  nor nor_4 (nor_4_out, in_8, in_8);
  nor nor_5 (nor_5_out, OR, in_10);
  nor nor_6 (out_17, nor_3_out, nor_4_out);
  nor nor_7 (out_18, nor_5_out, nor_5_out);
  Clock clock_1 (.out(clock_1_out));
  rs_agreg rs_agreg_1 (.R(in_3), .S(in_4), .Q(out_12), .Qbar(out_13));
  d_agreg d_agreg_1 (.D(in_6), .H(clock_1_out), .Q(out_15), .Qbar(out_16));

  // Notes on the sheet:
  //   NOT
  //   AND
endmodule

module rs_agreg (
  input  R,
  input  S,
  output Q,
  output Qbar
);

  nor nor_1 (Q, R, Qbar);
  nor nor_2 (Qbar, Q, S);

  // Notes on the sheet:
  //   BASCULE RS
endmodule

module d_agreg (
  input  H,
  input  D,
  output Q,
  output Qbar
);

  wire or_1_out, rs_agreg_1_qbar, rs_agreg_2_q, rs_agreg_2_qbar;

  or or_1 (or_1_out, rs_agreg_1_qbar, H);
  rs_agreg rs_agreg_1 (.R(rs_agreg_2_qbar), .S(H), .Qbar(rs_agreg_1_qbar));  // open: Q
  rs_agreg rs_agreg_2 (.R(or_1_out), .S(D), .Q(rs_agreg_2_q), .Qbar(rs_agreg_2_qbar));
  rs_agreg rs_agreg_3 (.R(rs_agreg_1_qbar), .S(rs_agreg_2_q), .Q(Q), .Qbar(Qbar));

  // Notes on the sheet:
  //   BASCULE D
endmodule

module automate_moore (
  input  Donne,
  output Sortie,
  output [2:0] Etat
);

  wire and_1_out, Horloge_out, nor_1_out, nor_2_out, or_1_out, or_2_out;

  D_Flip_Flop d_ff_1 (.D(Donne), .clk(Horloge_out), .Q(Etat[0]));  // open: Qn, preset, reset
  Clock Horloge (.out(Horloge_out));
  nor nor_1 (nor_1_out, Etat[1], Etat[2]);
  or or_1 (or_1_out, nor_1_out, Etat[0]);
  D_Flip_Flop d_ff_2 (.D(or_1_out), .clk(Horloge_out), .Q(Etat[1]));  // open: Qn, preset, reset
  or or_2 (or_2_out, Etat[2], Etat[1]);
  nor nor_2 (nor_2_out, Etat[0], Donne);
  D_Flip_Flop d_ff_3 (.D(and_1_out), .clk(Horloge_out), .Q(Etat[2]));  // open: Qn, preset, reset
  and and_1 (and_1_out, or_2_out, nor_2_out);
  XOR_avec_NOR xor_avec_nor_1 (.Q0(Etat[0]), .Q1(Etat[1]), .S(Sortie));

  // Notes on the sheet:
  //   Q0
  //   Q1
  //   Q2
endmodule

module XOR_avec_NOR (
  input  Q0,
  input  Q1,
  output S
);

  wire non_Q1_out, non_Q2_out, nor_1_out, nor_2_out, nor_3_out, nor_4_out, nor_5_out, nor_6_out;

  not non_Q1 (non_Q1_out, Q0);
  not non_Q2 (non_Q2_out, Q1);
  nor nor_1 (nor_1_out, Q0, Q1);
  nor nor_2 (nor_2_out, non_Q1_out, non_Q2_out);
  nor nor_3 (nor_3_out, nor_1_out, nor_1_out);
  nor nor_4 (nor_4_out, nor_2_out, nor_2_out);
  nor nor_5 (nor_5_out, nor_3_out, nor_3_out);
  nor nor_6 (nor_6_out, nor_4_out, nor_4_out);
  nor nor_7 (S, nor_5_out, nor_6_out);

  // Notes on the sheet:
  //   OR
  //   OR
  //   AND
endmodule
